// Logisim project 4_Bit_ALU.circ as structural Verilog: 1 circuit, main circuit main
module main (
  input  [3:0] B,
  input  [3:0] A,
  input  [2:0] ALUControl,
  output [3:0] out_4,
  output [3:0] out_5,
  output [3:0] ALUResult,
  output [3:0] out_7,
  output [3:0] out_8,
  output [3:0] out_9
);

  wire [3:0] multiplexer_1_out, not_1_out;

  assign not_1_out = ~B;  // NOT_Gate not_1, 4 bits wide
  Multiplexer #(.width(4)) multiplexer_1 (.in0(B), .in1(not_1_out), .out(multiplexer_1_out), .sel(ALUControl[0]));
  Adder #(.width(4)) adder_1 (.a(A), .b(multiplexer_1_out), .out(out_4), .cin(ALUControl[0]));  // open: cout
  assign out_5 = A & B;  // AND_Gate and_1, 4 bits wide
  assign out_7 = A | B;  // OR_Gate or_1, 4 bits wide
  assign out_8 = A ^ B;  // XOR_Gate xor_1, 4 bits wide
  assign out_9 = ~A;  // NOT_Gate not_2, 4 bits wide
  Multiplexer #(.select(3), .width(4)) multiplexer_2 (
    .in0(out_4), .in1(out_4), .in2(out_5), .in3(out_7), .in4(out_8), .in5(out_9), .out(ALUResult),
    .sel(ALUControl));  // open: in6, in7

  // Notes on the sheet:
  //   ALUControl: pull=up
endmodule
